// Logisim project Logic Project.circ as structural Verilog
module main (
  input  Op_Sel_0,
  input  Op_Sel_1,
  input  Num1_B0,
  input  Num1_B1,
  input  Num1_sgn,
  input  Num2_B0,
  input  Num2_B1,
  input  Num2_sgn,
  output Out_0,
  output Out_1,
  output Out_2,
  output Out_3,
  output Sign_Flag,
  output out_14,
  output out_15
);

  wire mux2_1_out_4, mux4_5_out_7, n2bitmod_1_out_5, n2bitmod_1_out_6, n2bitmod_1_out_7,
       n2bitmultiplayer_1_out_5, n2bitmultiplayer_1_out_6, n2bitmultiplayer_1_out_7,
       n2bitmultiplayer_1_out_8, n3bitaddsub_1_out_8, n3bitaddsub_1_out_9, n3bitaddsub_1_out_10,
       n3bitaddsub_1_out_11, not_1_out, not_2_out, not_3_out, not_4_out, not_5_out, xor_1_out, xor_2_out,
       xor_3_out, xor_4_out, xor_5_out;

  xor xor_1 (xor_1_out, Op_Sel_0, Num2_sgn);
  xor xor_2 (xor_2_out, Num1_sgn, xor_1_out);
  _2BitMod u_2bitmod_1 (
    .in_1(Num1_B0), .in_2(Num1_B1), .in_3(Num2_B0), .in_4(Num2_B1), .out_5(n2bitmod_1_out_5),
    .out_6(n2bitmod_1_out_6), .out_7(n2bitmod_1_out_7));
  _3BitAddSub u_3bitaddsub_1 (
    .in_1(xor_2_out), .in_2(Num1_B0), .in_3(Num1_B1), .in_4(1'b0), .in_5(Num2_B0), .in_6(Num2_B1),
    .in_7(1'b0), .out_8(n3bitaddsub_1_out_8), .out_9(n3bitaddsub_1_out_9), .out_10(n3bitaddsub_1_out_10),
    .out_11(n3bitaddsub_1_out_11));
  _2BitMultiplayer u_2bitmultiplayer_1 (
    .in_1(Num1_B0), .in_2(Num1_B1), .in_3(Num2_B0), .in_4(Num2_B1), .out_5(n2bitmultiplayer_1_out_5),
    .out_6(n2bitmultiplayer_1_out_6), .out_7(n2bitmultiplayer_1_out_7), .out_8(n2bitmultiplayer_1_out_8));
  xor xor_3 (xor_3_out, Num2_sgn, Num1_sgn);
  xor xor_4 (xor_4_out, Num1_sgn, xor_1_out);
  xor xor_5 (xor_5_out, n3bitaddsub_1_out_11, Num1_sgn);
  MUX2 mux2_1 (.in_1(Num1_sgn), .in_2(xor_5_out), .in_3(xor_4_out), .out_4(mux2_1_out_4));
  MUX4 mux4_1 (
    .in_1(n3bitaddsub_1_out_8), .in_2(n3bitaddsub_1_out_8), .in_3(n2bitmultiplayer_1_out_5),
    .in_4(n2bitmod_1_out_5), .in_5(Op_Sel_0), .in_6(Op_Sel_1), .out_7(Out_0));
  MUX4 mux4_2 (
    .in_1(n3bitaddsub_1_out_9), .in_2(n3bitaddsub_1_out_9), .in_3(n2bitmultiplayer_1_out_6),
    .in_4(n2bitmod_1_out_6), .in_5(Op_Sel_0), .in_6(Op_Sel_1), .out_7(Out_1));
  MUX4 mux4_3 (
    .in_1(n3bitaddsub_1_out_10), .in_2(n3bitaddsub_1_out_10), .in_3(n2bitmultiplayer_1_out_7), .in_4(1'b0),
    .in_5(Op_Sel_0), .in_6(Op_Sel_1), .out_7(Out_2));
  MUX4 mux4_4 (
    .in_1(1'b0), .in_2(1'b0), .in_3(n2bitmultiplayer_1_out_8), .in_4(1'b0), .in_5(Op_Sel_0), .in_6(Op_Sel_1),
    .out_7(Out_3));
  MUX4 mux4_5 (
    .in_1(mux2_1_out_4), .in_2(mux2_1_out_4), .in_3(xor_3_out), .in_4(Num1_sgn), .in_5(Op_Sel_0),
    .in_6(Op_Sel_1), .out_7(mux4_5_out_7));
  MUX4 mux4_6 (
    .in_1(1'b0), .in_2(1'b0), .in_3(1'b0), .in_4(n2bitmod_1_out_7), .in_5(Op_Sel_0), .in_6(Op_Sel_1),
    .out_7(out_15));
  and and_1 (Sign_Flag, mux4_5_out_7, not_1_out);
  not not_1 (not_1_out, out_14);
  not not_2 (not_2_out, Out_0);
  not not_3 (not_3_out, Out_1);
  and and_2 (out_14, not_2_out, not_3_out, not_4_out, not_5_out);
  not not_4 (not_4_out, Out_2);
  not not_5 (not_5_out, Out_3);

  // Notes on the sheet:
  //   Result
  //   Zero Result
endmodule

module _1BitAdder (
  input  A,
  input  B,
  input  C,
  output Result,
  output Carry
);

  wire and_1_out, and_2_out, or_1_out, xor_1_out;

  xor xor_1 (xor_1_out, A, B);
  and and_1 (and_1_out, A, B);
  or or_1 (or_1_out, A, B);
  xor xor_2 (Result, xor_1_out, C);
  and and_2 (and_2_out, C, or_1_out);
  or or_2 (Carry, and_1_out, and_2_out);
endmodule

module _3BitAdder (
  input  First_Number,
  input  in_2,
  input  in_3,
  input  Second_Number,
  input  in_5,
  input  in_6,
  output out_7,
  output out_8,
  output out_9,
  output out_10
);

  wire n1bitadder_1_carry, n1bitadder_2_carry;

  _1BitAdder u_1bitadder_1 (.A(First_Number), .B(Second_Number), .C(1'b0), .Result(out_7), .Carry(n1bitadder_1_carry));
  _1BitAdder u_1bitadder_2 (.A(in_2), .B(in_5), .C(n1bitadder_1_carry), .Result(out_8), .Carry(n1bitadder_2_carry));
  _1BitAdder u_1bitadder_3 (.A(in_3), .B(in_6), .C(n1bitadder_2_carry), .Result(out_9), .Carry(out_10));
endmodule

// A/S
module _3BitAddSub (
  input  in_1,
  input  in_2,
  input  in_3,
  input  in_4,
  input  in_5,
  input  in_6,
  input  in_7,
  output out_8,
  output out_9,
  output out_10,
  output out_11
);

  wire mux2_1_out_4, mux2_2_out_4, mux2_3_out_4, n1bitadder_1_carry, n1bitadder_1_result, n1bitadder_2_carry,
       n1bitadder_2_result, n1bitadder_3_carry, n1bitadder_3_result, n1bitadder_4_carry, n1bitadder_4_result,
       n1bitadder_5_carry, n1bitadder_5_result, n1bitadder_6_result, not_1_out, not_2_out, not_3_out,
       not_4_out, xor_1_out, xor_2_out, xor_3_out;

  xor xor_1 (xor_1_out, in_1, in_5);
  xor xor_2 (xor_2_out, in_1, in_6);
  xor xor_3 (xor_3_out, in_1, in_7);
  _1BitAdder u_1bitadder_1 (
    .A(xor_1_out), .B(in_2), .C(in_1), .Result(n1bitadder_1_result), .Carry(n1bitadder_1_carry));
  _1BitAdder u_1bitadder_2 (
    .A(n1bitadder_1_carry), .B(in_3), .C(xor_2_out), .Result(n1bitadder_2_result), .Carry(n1bitadder_2_carry));
  _1BitAdder u_1bitadder_3 (
    .A(n1bitadder_2_carry), .B(in_4), .C(xor_3_out), .Result(n1bitadder_3_result), .Carry(n1bitadder_3_carry));
  not not_1 (not_1_out, n1bitadder_3_carry);
  not not_2 (not_2_out, n1bitadder_1_result);
  not not_3 (not_3_out, n1bitadder_2_result);
  not not_4 (not_4_out, n1bitadder_3_result);
  _1BitAdder u_1bitadder_4 (
    .A(not_2_out), .B(1'b1), .C(1'b0), .Result(n1bitadder_4_result), .Carry(n1bitadder_4_carry));
  _1BitAdder u_1bitadder_5 (
    .A(n1bitadder_4_carry), .B(not_3_out), .C(1'b0), .Result(n1bitadder_5_result), .Carry(n1bitadder_5_carry));
  _1BitAdder u_1bitadder_6 (
    .A(n1bitadder_5_carry), .B(not_4_out), .C(1'b0), .Result(n1bitadder_6_result));  // open: Carry
  MUX2 mux2_1 (.in_1(n1bitadder_1_result), .in_2(n1bitadder_4_result), .in_3(not_1_out), .out_4(mux2_1_out_4));
  MUX2 mux2_2 (.in_1(n1bitadder_2_result), .in_2(n1bitadder_5_result), .in_3(not_1_out), .out_4(mux2_2_out_4));
  MUX2 mux2_3 (.in_1(n1bitadder_3_result), .in_2(n1bitadder_6_result), .in_3(not_1_out), .out_4(mux2_3_out_4));
  MUX2 mux2_4 (.in_1(n1bitadder_1_result), .in_2(mux2_1_out_4), .in_3(in_1), .out_4(out_8));
  MUX2 mux2_5 (.in_1(n1bitadder_2_result), .in_2(mux2_2_out_4), .in_3(in_1), .out_4(out_9));
  MUX2 mux2_6 (.in_1(n1bitadder_3_result), .in_2(mux2_3_out_4), .in_3(in_1), .out_4(out_10));
  MUX2 mux2_7 (.in_1(n1bitadder_3_carry), .in_2(not_1_out), .in_3(in_1), .out_4(out_11));

  // Notes on the sheet:
  //   Num 1
  //   Num 2
  //   Operation Selection 
endmodule

module MUX2 (
  input  in_1,
  input  in_2,
  input  in_3,
  output out_4
);

  wire and_1_out, and_2_out, not_1_out;

  not not_1 (not_1_out, in_3);
  and and_1 (and_1_out, in_1, not_1_out);
  and and_2 (and_2_out, in_2, in_3);
  or or_1 (out_4, and_1_out, and_2_out);
endmodule

module MUX4 (
  input  in_1,
  input  in_2,
  input  in_3,
  input  in_4,
  input  in_5,
  input  in_6,
  output out_7
);

  wire mux2_1_out_4, mux2_2_out_4;

  MUX2 mux2_1 (.in_1(in_1), .in_2(in_2), .in_3(in_5), .out_4(mux2_1_out_4));
  MUX2 mux2_2 (.in_1(in_3), .in_2(in_4), .in_3(in_5), .out_4(mux2_2_out_4));
  MUX2 mux2_3 (.in_1(mux2_1_out_4), .in_2(mux2_2_out_4), .in_3(in_6), .out_4(out_7));
endmodule

// MUL
module _2BitMultiplayer (
  input  in_1,
  input  in_2,
  input  in_3,
  input  in_4,
  output out_5,
  output out_6,
  output out_7,
  output out_8
);

  wire and_1_out, and_2_out, and_3_out, and_4_out;

  and and_1 (and_1_out, in_1, in_3);
  and and_2 (and_2_out, in_2, in_3);
  and and_3 (and_3_out, in_1, in_4);
  and and_4 (and_4_out, in_2, in_4);
  _3BitAdder u_3bitadder_1 (
    .First_Number(and_1_out), .in_2(and_2_out), .in_3(1'b0), .Second_Number(1'b0), .in_5(and_3_out),
    .in_6(and_4_out), .out_7(out_5), .out_8(out_6), .out_9(out_7), .out_10(out_8));
endmodule

module Unsinged2BitAdder (
  input  in_1,
  input  in_2,
  input  in_3,
  input  in_4,
  output out_5,
  output out_6,
  output out_7
);

  wire n1bitadder_1_carry;

  _1BitAdder u_1bitadder_1 (.A(in_1), .B(in_3), .C(1'b0), .Result(out_5), .Carry(n1bitadder_1_carry));
  _1BitAdder u_1bitadder_2 (.A(n1bitadder_1_carry), .B(in_2), .C(in_4), .Result(out_6), .Carry(out_7));
endmodule

// MOD
module _2BitMod (
  input  in_1,
  input  in_2,
  input  in_3,
  input  in_4,
  output out_5,
  output out_6,
  output out_7
);

  wire mux2_1_out_4, mux2_2_out_4, nand_1_out;

  nand nand_1 (nand_1_out, in_2, in_1);
  MUX2 mux2_1 (.in_1(1'b0), .in_2(in_1), .in_3(nand_1_out), .out_4(mux2_1_out_4));
  MUX2 mux2_2 (.in_1(1'b0), .in_2(in_2), .in_3(nand_1_out), .out_4(mux2_2_out_4));
  MUX4 mux4_1 (.in_1(1'b0), .in_2(1'b0), .in_3(in_1), .in_4(mux2_1_out_4), .in_5(in_3), .in_6(in_4), .out_7(out_5));
  MUX4 mux4_2 (.in_1(1'b0), .in_2(1'b0), .in_3(1'b0), .in_4(mux2_2_out_4), .in_5(in_3), .in_6(in_4), .out_7(out_6));
  MUX4 mux4_3 (.in_1(1'b1), .in_2(1'b0), .in_3(1'b0), .in_4(1'b0), .in_5(in_3), .in_6(in_4), .out_7(out_7));
endmodule

// A/S
module _2BitAddSub (
  input  in_1,
  input  in_2,
  input  in_3,
  input  in_4,
  input  in_5,
  output out_6,
  output out_7,
  output out_8
);

  wire mux2_1_out_4, mux2_2_out_4, n1bitadder_1_carry, n1bitadder_1_result, n1bitadder_2_carry,
       n1bitadder_2_result, n1bitadder_3_carry, n1bitadder_3_result, n1bitadder_4_result, not_1_out,
       not_2_out, not_3_out, xor_1_out, xor_2_out;

  xor xor_1 (xor_1_out, in_1, in_4);
  xor xor_2 (xor_2_out, in_1, in_5);
  _1BitAdder u_1bitadder_1 (
    .A(in_1), .B(in_2), .C(xor_1_out), .Result(n1bitadder_1_result), .Carry(n1bitadder_1_carry));
  _1BitAdder u_1bitadder_2 (
    .A(n1bitadder_1_carry), .B(in_3), .C(xor_2_out), .Result(n1bitadder_2_result), .Carry(n1bitadder_2_carry));
  not not_1 (not_1_out, n1bitadder_2_carry);
  not not_2 (not_2_out, n1bitadder_1_result);
  not not_3 (not_3_out, n1bitadder_2_result);
  _1BitAdder u_1bitadder_3 (
    .A(1'b1), .B(not_2_out), .C(1'b0), .Result(n1bitadder_3_result), .Carry(n1bitadder_3_carry));
  _1BitAdder u_1bitadder_4 (
    .A(n1bitadder_3_carry), .B(not_3_out), .C(1'b0), .Result(n1bitadder_4_result));  // open: Carry
  MUX2 mux2_1 (.in_1(n1bitadder_1_result), .in_2(n1bitadder_3_result), .in_3(not_1_out), .out_4(mux2_1_out_4));
  MUX2 mux2_2 (.in_1(n1bitadder_2_result), .in_2(n1bitadder_4_result), .in_3(not_1_out), .out_4(mux2_2_out_4));
  MUX2 mux2_3 (.in_1(n1bitadder_1_result), .in_2(mux2_1_out_4), .in_3(in_1), .out_4(out_6));
  MUX2 mux2_4 (.in_1(n1bitadder_2_result), .in_2(mux2_2_out_4), .in_3(in_1), .out_4(out_7));
  MUX2 mux2_5 (.in_1(n1bitadder_2_carry), .in_2(not_1_out), .in_3(in_1), .out_4(out_8));

  // Notes on the sheet:
  //   Operation Selection 
endmodule

// MAIN
module main_opt (
  input  Operation_Select,
  input  in_2,
  input  Num1__B0_B1_SGN,
  input  in_4,
  input  in_5,
  input  Num2__B0_B1_SGN,
  input  in_7,
  input  in_8,
  output out_9,
  output out_10,
  output out_11,
  output out_12,
  output Sign,
  output IsZero,
  output Error
);

  wire and_1_out, mux4_5_out_7, n2bitaddsub_s_opt_d1_1_out_8, n2bitaddsub_s_opt_d1_1_out_9,
       n2bitaddsub_s_opt_d1_1_out_10, n2bitaddsub_s_opt_d1_1_out_11, n2bitmod_opt_1_out_5,
       n2bitmod_opt_1_out_6, n2bitmod_opt_1_out_7, n2bitmultiplayer_1_out_5, n2bitmultiplayer_1_out_6,
       n2bitmultiplayer_1_out_7, n2bitmultiplayer_1_out_8, not_1_out, xor_1_out;

  xor xor_1 (xor_1_out, in_8, in_5);
  _2BitAddSub_S_Opt_D1 u_2bitaddsub_s_opt_d1_1 (
    .in_1(Operation_Select), .in_2(Num1__B0_B1_SGN), .in_3(in_4), .in_4(in_5), .in_5(Num2__B0_B1_SGN),
    .in_6(in_7), .in_7(in_8), .out_8(n2bitaddsub_s_opt_d1_1_out_8), .out_9(n2bitaddsub_s_opt_d1_1_out_9),
    .out_10(n2bitaddsub_s_opt_d1_1_out_10), .out_11(n2bitaddsub_s_opt_d1_1_out_11));
  _2BitMultiplayer u_2bitmultiplayer_1 (
    .in_1(Num1__B0_B1_SGN), .in_2(in_4), .in_3(Num2__B0_B1_SGN), .in_4(in_7),
    .out_5(n2bitmultiplayer_1_out_5), .out_6(n2bitmultiplayer_1_out_6), .out_7(n2bitmultiplayer_1_out_7),
    .out_8(n2bitmultiplayer_1_out_8));
  _2BitMod_opt u_2bitmod_opt_1 (
    .in_1(Num1__B0_B1_SGN), .in_2(in_4), .in_3(Num2__B0_B1_SGN), .in_4(in_7), .out_5(n2bitmod_opt_1_out_5),
    .out_6(n2bitmod_opt_1_out_6), .out_7(n2bitmod_opt_1_out_7));
  and and_1 (and_1_out, in_2, Operation_Select);
  MUX4 mux4_1 (
    .in_1(n2bitaddsub_s_opt_d1_1_out_8), .in_2(n2bitaddsub_s_opt_d1_1_out_8),
    .in_3(n2bitmultiplayer_1_out_5), .in_4(n2bitmod_opt_1_out_5), .in_5(Operation_Select), .in_6(in_2),
    .out_7(out_9));
  MUX4 mux4_2 (
    .in_1(n2bitaddsub_s_opt_d1_1_out_9), .in_2(n2bitaddsub_s_opt_d1_1_out_9),
    .in_3(n2bitmultiplayer_1_out_6), .in_4(n2bitmod_opt_1_out_6), .in_5(Operation_Select), .in_6(in_2),
    .out_7(out_10));
  MUX4 mux4_3 (
    .in_1(n2bitaddsub_s_opt_d1_1_out_10), .in_2(n2bitaddsub_s_opt_d1_1_out_10),
    .in_3(n2bitmultiplayer_1_out_7), .in_4(1'b0), .in_5(Operation_Select), .in_6(in_2), .out_7(out_11));
  MUX4 mux4_4 (
    .in_1(1'b0), .in_2(1'b0), .in_3(n2bitmultiplayer_1_out_8), .in_4(1'b0), .in_5(Operation_Select),
    .in_6(in_2), .out_7(out_12));
  MUX4 mux4_5 (
    .in_1(n2bitaddsub_s_opt_d1_1_out_11), .in_2(n2bitaddsub_s_opt_d1_1_out_11), .in_3(xor_1_out),
    .in_4(in_5), .in_5(Operation_Select), .in_6(in_2), .out_7(mux4_5_out_7));
  and and_2 (Error, and_1_out, n2bitmod_opt_1_out_7);
  not not_1 (not_1_out, IsZero);
  nor nor_1 (IsZero, out_9, out_10, out_11, out_12);
  and and_3 (Sign, mux4_5_out_7, not_1_out);

  // Notes on the sheet:
  //   Operations: 0 add , 1 sub , 2 Mul , 3 Mod
  //   Result
endmodule

// MOD
module _2BitMod_opt (
  input  in_1,
  input  in_2,
  input  in_3,
  input  in_4,
  output out_5,
  output out_6,
  output out_7
);

  wire and_1_out, and_2_out, and_3_out, and_4_out, and_6_out, and_7_out, not_1_out, not_2_out, not_3_out,
       not_4_out, not_5_out;

  and and_1 (and_1_out, in_1, not_1_out);
  not not_1 (not_1_out, in_2);
  and and_2 (and_2_out, in_1, not_2_out);
  not not_2 (not_2_out, in_3);
  not not_3 (not_3_out, in_1);
  and and_3 (and_3_out, not_3_out, in_2);
  and and_4 (and_4_out, in_3, in_4);
  not not_4 (not_4_out, in_3);
  and and_5 (out_7, not_4_out, not_5_out);
  not not_5 (not_5_out, in_4);
  and and_6 (and_6_out, and_1_out, in_4);
  and and_7 (and_7_out, and_2_out, in_4);
  and and_8 (out_6, and_3_out, and_4_out);
  or or_1 (out_5, and_6_out, and_7_out);
endmodule

module main_on_display (
  input  in_1,
  input  NUM1,
  input  in_3,
  input  in_4,
  input  in_5,
  input  in_6,
  input  NUM2,
  input  in_8,
  output out_9,
  output out_10,
  output Result,
  output out_12,
  output out_13,
  output IsZero,
  output Error
);

  wire n7_segment_display_driver_1_p1, n7_segment_display_driver_1_p2, n7_segment_display_driver_1_p3,
       n7_segment_display_driver_1_p5, n7_segment_display_driver_1_p7, n7_segment_display_driver_1_p9,
       n7_segment_display_driver_1_p11, n7_segment_display_driver_2_p1, n7_segment_display_driver_2_p2,
       n7_segment_display_driver_2_p3, n7_segment_display_driver_2_p5, n7_segment_display_driver_2_p7,
       n7_segment_display_driver_2_p9, n7_segment_display_driver_2_p11, n7_sig_errorable_1_out_6,
       n7_sig_errorable_1_out_7, n7_sig_errorable_1_out_8, n7_sig_errorable_1_out_9,
       n7_sig_errorable_1_out_10, n7_sig_errorable_1_out_11, n7_sig_errorable_1_out_12, not_1_out;
  wire [2:0] graphical_unit_software_only_1_out_3, graphical_unit_software_only_1_out_4,
       graphical_unit_software_only_1_out_5;

  _7_Segment_Display u_7_segment_display_1 (.g(in_1));  // open: f, a, b, e, d, c, dp
  _7_Segment_Display u_7_segment_display_2 (
    .g(n7_segment_display_driver_1_p1), .f(n7_segment_display_driver_1_p2),
    .a(n7_segment_display_driver_1_p11), .b(n7_segment_display_driver_1_p9),
    .e(n7_segment_display_driver_1_p3), .d(n7_segment_display_driver_1_p5), .c(n7_segment_display_driver_1_p7));  // open: dp
  // _7_segment_display_driver 7_segment_display_driver_1: pin names not known; wires that end beside it: n7_segment_display_driver_1_p1, n7_segment_display_driver_1_p2, n7_segment_display_driver_1_p3, in_3, n7_segment_display_driver_1_p5, NUM1, n7_segment_display_driver_1_p7, 1'b0, n7_segment_display_driver_1_p9, 1'b0, n7_segment_display_driver_1_p11
  graphical_unit__software_only graphical_unit_software_only_1 (
    .in_1(in_5), .in_2(in_4), .out_3(graphical_unit_software_only_1_out_3),
    .out_4(graphical_unit_software_only_1_out_4), .out_5(graphical_unit_software_only_1_out_5));
  DotMatrix #(.inputtype("row"), .matrixcols(3), .matrixrows(3)) dotmatrix_1 (
    .row0(graphical_unit_software_only_1_out_3), .row1(graphical_unit_software_only_1_out_4),
    .row2(graphical_unit_software_only_1_out_5));
  _7_Segment_Display u_7_segment_display_3 (.g(in_6));  // open: f, a, b, e, d, c, dp
  _7_Segment_Display u_7_segment_display_4 (
    .g(n7_segment_display_driver_2_p1), .f(n7_segment_display_driver_2_p2),
    .a(n7_segment_display_driver_2_p11), .b(n7_segment_display_driver_2_p9),
    .e(n7_segment_display_driver_2_p3), .d(n7_segment_display_driver_2_p5), .c(n7_segment_display_driver_2_p7));  // open: dp
  // _7_segment_display_driver 7_segment_display_driver_2: pin names not known; wires that end beside it: n7_segment_display_driver_2_p1, n7_segment_display_driver_2_p2, n7_segment_display_driver_2_p3, in_8, n7_segment_display_driver_2_p5, NUM2, n7_segment_display_driver_2_p7, 1'b0, n7_segment_display_driver_2_p9, 1'b0, n7_segment_display_driver_2_p11
  main_opt main_opt_1 (
    .Operation_Select(in_5), .in_2(in_4), .Num1__B0_B1_SGN(in_3), .in_4(NUM1), .in_5(in_1),
    .Num2__B0_B1_SGN(in_8), .in_7(NUM2), .in_8(in_6), .out_9(out_13), .out_10(out_12), .out_11(Result),
    .out_12(out_10), .Sign(out_9), .IsZero(IsZero), .Error(Error));
  _7_Segment_Display u_7_segment_display_5 (.g(out_9));  // open: f, a, b, e, d, c, dp
  _7_sig_errorable u_7_sig_errorable_1 (
    .in_1(out_10), .in_2(Result), .in_3(out_12), .in_4(out_13), .in_5(not_1_out),
    .out_6(n7_sig_errorable_1_out_6), .out_7(n7_sig_errorable_1_out_7), .out_8(n7_sig_errorable_1_out_8),
    .out_9(n7_sig_errorable_1_out_9), .out_10(n7_sig_errorable_1_out_10), .out_11(n7_sig_errorable_1_out_11),
    .out_12(n7_sig_errorable_1_out_12));
  _7_Segment_Display u_7_segment_display_6 (
    .g(n7_sig_errorable_1_out_12), .f(n7_sig_errorable_1_out_11), .a(n7_sig_errorable_1_out_6),
    .b(n7_sig_errorable_1_out_7), .e(n7_sig_errorable_1_out_10), .d(n7_sig_errorable_1_out_9),
    .c(n7_sig_errorable_1_out_8));  // open: dp
  not not_1 (not_1_out, Error);
  LED led_1 (.in(IsZero));
  // Simple_buzzer simple_buzzer_1: pin names not known; wires that end beside it: Error, 1'b1

  // Notes on the sheet:
  //   Operation
endmodule

module _7_sig_errorable (
  input  in_1,
  input  in_2,
  input  in_3,
  input  in_4,
  input  in_5,
  output out_6,
  output out_7,
  output out_8,
  output out_9,
  output out_10,
  output out_11,
  output out_12
);

  wire n7_segment_display_driver_1_p5, n7_segment_display_driver_1_p6, n7_segment_display_driver_1_p7,
       n7_segment_display_driver_1_p8, n7_segment_display_driver_1_p9, n7_segment_display_driver_1_p10,
       n7_segment_display_driver_1_p11;

  // _7_segment_display_driver 7_segment_display_driver_1: pin names not known; wires that end beside it: in_1, in_2, in_3, in_4, n7_segment_display_driver_1_p5, n7_segment_display_driver_1_p6, n7_segment_display_driver_1_p7, n7_segment_display_driver_1_p8, n7_segment_display_driver_1_p9, n7_segment_display_driver_1_p10, n7_segment_display_driver_1_p11
  and and_1 (out_6, n7_segment_display_driver_1_p5, in_5);
  and and_2 (out_7, n7_segment_display_driver_1_p6, in_5);
  and and_3 (out_8, n7_segment_display_driver_1_p7, in_5);
  and and_4 (out_9, n7_segment_display_driver_1_p8, in_5);
  and and_5 (out_10, n7_segment_display_driver_1_p9, in_5);
  and and_6 (out_11, n7_segment_display_driver_1_p10, in_5);
  and and_7 (out_12, n7_segment_display_driver_1_p11, in_5);
endmodule

module _2BitAddSub_US_Opt (
  input  in_1,
  input  in_2,
  input  in_3,
  input  in_4,
  input  in_5,
  output out_6,
  output out_7,
  output out_8,
  output out_9
);

  wire and_1_out, n1bitadder_1_carry, n1bitadder_1_result, n1bitadder_2_carry, n1bitadder_2_result,
       n1bitadder_3_carry, not_1_out, not_2_out, xor_1_out, xor_2_out, xor_3_out, xor_4_out;

  xor xor_1 (xor_1_out, in_1, in_4);
  xor xor_2 (xor_2_out, in_1, in_5);
  _1BitAdder u_1bitadder_1 (
    .A(in_1), .B(in_2), .C(xor_1_out), .Result(n1bitadder_1_result), .Carry(n1bitadder_1_carry));
  _1BitAdder u_1bitadder_2 (
    .A(n1bitadder_1_carry), .B(in_3), .C(xor_2_out), .Result(n1bitadder_2_result), .Carry(n1bitadder_2_carry));
  not not_1 (not_1_out, n1bitadder_2_carry);
  xor xor_3 (xor_3_out, n1bitadder_2_result, and_1_out);
  xor xor_4 (xor_4_out, n1bitadder_1_result, and_1_out);
  and and_1 (and_1_out, not_1_out, in_1);
  _1BitAdder u_1bitadder_3 (.A(and_1_out), .B(xor_4_out), .C(1'b0), .Result(out_6), .Carry(n1bitadder_3_carry));
  _1BitAdder u_1bitadder_4 (.A(n1bitadder_3_carry), .B(xor_3_out), .C(1'b0), .Result(out_7));  // open: Carry
  and and_2 (out_8, n1bitadder_2_carry, not_2_out);
  not not_2 (not_2_out, in_1);
  and and_3 (out_9, in_1, not_1_out);

  // Notes on the sheet:
  //   Operation Selection 
endmodule

// 2BASF
module _2BitAddSub_S_Opt_D1 (
  input  in_1,
  input  in_2,
  input  in_3,
  input  in_4,
  input  in_5,
  input  in_6,
  input  in_7,
  output out_8,
  output out_9,
  output out_10,
  output out_11
);

  wire n2bitaddsub_us_opt_1_out_9, xor_1_out, xor_2_out;

  xor xor_1 (xor_1_out, in_1, in_7);
  xor xor_2 (xor_2_out, xor_1_out, in_4);
  _2BitAddSub_US_Opt u_2bitaddsub_us_opt_1 (
    .in_1(xor_2_out), .in_2(in_2), .in_3(in_3), .in_4(in_5), .in_5(in_6), .out_6(out_8), .out_7(out_9),
    .out_8(out_10), .out_9(n2bitaddsub_us_opt_1_out_9));
  xor xor_3 (out_11, n2bitaddsub_us_opt_1_out_9, in_4);
endmodule

module graphical_unit__software_only (
  input  in_1,
  input  in_2,
  output [2:0] out_3,
  output [2:0] out_4,
  output [2:0] out_5
);

  MUX4 mux4_1 (.in_1(1'b0), .in_2(1'b0), .in_3(1'b1), .in_4(1'b0), .in_5(in_1), .in_6(in_2), .out_7(out_3[0]));
  MUX4 mux4_2 (.in_1(1'b1), .in_2(1'b1), .in_3(1'b0), .in_4(1'b0), .in_5(in_1), .in_6(in_2), .out_7(out_4[0]));
  MUX4 mux4_3 (.in_1(1'b0), .in_2(1'b0), .in_3(1'b1), .in_4(1'b1), .in_5(in_1), .in_6(in_2), .out_7(out_5[0]));
  MUX4 mux4_4 (.in_1(1'b1), .in_2(1'b0), .in_3(1'b0), .in_4(1'b0), .in_5(in_1), .in_6(in_2), .out_7(out_3[1]));
  MUX4 mux4_5 (.in_1(1'b1), .in_2(1'b0), .in_3(1'b0), .in_4(1'b0), .in_5(in_1), .in_6(in_2), .out_7(out_5[1]));
  MUX4 mux4_6 (.in_1(1'b0), .in_2(1'b0), .in_3(1'b1), .in_4(1'b1), .in_5(in_1), .in_6(in_2), .out_7(out_3[2]));
  MUX4 mux4_7 (.in_1(1'b1), .in_2(1'b1), .in_3(1'b0), .in_4(1'b0), .in_5(in_1), .in_6(in_2), .out_7(out_4[2]));
  MUX4 mux4_8 (.in_1(1'b0), .in_2(1'b0), .in_3(1'b1), .in_4(1'b0), .in_5(in_1), .in_6(in_2), .out_7(out_5[2]));

  assign out_4[1] = 1'b1;
endmodule

module _2BitMod_EX (
  input  in_1,
  input  in_2,
  input  in_3,
  input  in_4,
  output out_5,
  output out_6,
  output out_7
);

  wire mux2_1_out_4, mux2_2_out_4, n2bitaddsub_us_opt_1_out_6, n2bitaddsub_us_opt_1_out_7,
       n2bitaddsub_us_opt_1_out_9, nand_1_out, not_1_out, not_2_out;

  nand nand_1 (nand_1_out, in_3, not_1_out);
  not not_1 (not_1_out, in_4);
  _2BitAddSub_US_Opt u_2bitaddsub_us_opt_1 (
    .in_1(1'b1), .in_2(in_1), .in_3(in_2), .in_4(in_3), .in_5(in_4), .out_6(n2bitaddsub_us_opt_1_out_6),
    .out_7(n2bitaddsub_us_opt_1_out_7), .out_9(n2bitaddsub_us_opt_1_out_9));  // open: out_8
  not not_2 (not_2_out, n2bitaddsub_us_opt_1_out_9);
  MUX2 mux2_1 (.in_1(in_1), .in_2(n2bitaddsub_us_opt_1_out_6), .in_3(not_2_out), .out_4(mux2_1_out_4));
  MUX2 mux2_2 (.in_1(in_2), .in_2(n2bitaddsub_us_opt_1_out_7), .in_3(not_2_out), .out_4(mux2_2_out_4));
  and and_1 (out_5, mux2_1_out_4, nand_1_out);
  and and_2 (out_6, mux2_2_out_4, nand_1_out);
  nor nor_1 (out_7, in_3, in_4);
endmodule
